// Logisim project Lab 11.circ as structural Verilog: 1 circuit, main circuit main
module main (
  input  Tank_A_Low_Level_Switch_Logic_1_for_low_level,
  input  Tank_B_Low_Level_Switch_Logic_1_for_low_level,
  input  Tank_C_Low_Level_Switch_Logic_1_for_low_level,
  input  Silence_Switch___Logic_1_when_switch_is_in_silence_position
);

  wire and_1_out, and_2_out, and_3_out, and_4_out, not_1_out, or_1_out;

  not not_1 (not_1_out, Silence_Switch___Logic_1_when_switch_is_in_silence_position);
  and and_1 (and_1_out, Tank_A_Low_Level_Switch_Logic_1_for_low_level, Tank_B_Low_Level_Switch_Logic_1_for_low_level);
  and and_2 (and_2_out, Tank_A_Low_Level_Switch_Logic_1_for_low_level, Tank_C_Low_Level_Switch_Logic_1_for_low_level);
  and and_3 (and_3_out, Tank_B_Low_Level_Switch_Logic_1_for_low_level, Tank_C_Low_Level_Switch_Logic_1_for_low_level);
  or or_1 (or_1_out, and_1_out, and_2_out, and_3_out);
  LED led_1 (.in(and_4_out));
  and and_4 (and_4_out, or_1_out, not_1_out);
endmodule
