// Logisim project Lab 12.2.circ as structural Verilog: 1 circuit, main circuit main
module main (
  input  A,
  input  B,
  input  C,
  output X
);

  wire not_1_out, not_2_out, not_3_out, or_1_out, or_2_out, or_3_out, or_4_out;

  not not_1 (not_1_out, B);
  not not_2 (not_2_out, A);
  not not_3 (not_3_out, C);
  or or_1 (or_1_out, A, B, C);
  or or_2 (or_2_out, A, not_3_out, not_1_out);
  or or_3 (or_3_out, not_2_out, not_1_out, C);
  or or_4 (or_4_out, not_2_out, not_1_out, not_3_out);
  and and_1 (X, or_1_out, or_2_out, or_3_out, or_4_out);
endmodule
