// Logisim project Lab 12.3.circ as structural Verilog: 1 circuit, main circuit main
module main (
  input  A,
  input  B,
  input  C,
  output X
);

  wire and_1_out, and_2_out, and_3_out, and_4_out, not_1_out, not_2_out, not_3_out, or_1_out;

  not not_1 (not_1_out, B);
  not not_2 (not_2_out, C);
  not not_3 (not_3_out, A);
  and and_1 (and_1_out, not_3_out, not_1_out, not_2_out);
  and and_2 (and_2_out, not_3_out, B, C);
  and and_3 (and_3_out, A, B, not_2_out);
  and and_4 (and_4_out, A, B, C);
  or or_1 (or_1_out, and_1_out, and_2_out, and_3_out, and_4_out);
  not not_4 (X, or_1_out);
endmodule
