// Logisim project Lab 8.circ as structural Verilog: 1 circuit, main circuit main
module main (
  input  A,
  input  B,
  input  C
);

  wire and_1_out, not_1_out, or_1_out;

  not not_1 (not_1_out, A);
  // Probe on not_1_out
  and and_1 (and_1_out, not_1_out, B);
  // Probe on nothing
  or or_1 (or_1_out, and_1_out, C);
  // Probe on nothing
endmodule
